# Fritzing sketch SlowMotionShowdown (saved by Fritzing 1.0.1rc)
breadboards: 3

parts:
  A1 = Particle - Photon2
  S7 = Pushbutton [package="[THT]"]
  S8 = Pushbutton [package="[THT]"]
  S9 = Pushbutton [package="[THT]"]
  S10 = Pushbutton [package="[THT]"]
  S5 = Pushbutton [package="[THT]"]
  Part1 = HC-SR501 Body Sensor Module
  Part2 = HC-SR501 Body Sensor Module
  Neopixel2 = Adafruit RBG Smart Neopixel [package="DIP (Dual Inline) [THT]"]
  OLED_I2C1 = OLED 128x64 I2C Monochrome Display
  S11 = Taiway 100-SP-X-T1 SPDT Miniature Toggle Switch [part_number=100-SP-X-T1-0-0-B1-M2 package=THT]
  S12 = Pushbutton [package="[THT]"]
  LED1 = LED - 5mm [color="White (6500K)" current=0.030A package="5 mm [THT]"]
  LED2 = LED - 5mm [color="White (6500K)" current=0.030A package="5 mm [THT]"]
  LED3 = LED - 5mm [color="White (6500K)" current=0.030A package="5 mm [THT]"]
  LED4 = LED - 5mm [color="White (6500K)" current=0.030A package="5 mm [THT]"]
  Neopixel1 = Adafruit RBG Smart Neopixel [package="DIP (Dual Inline) [THT]"]
  LED5 = LED - 5mm [color="Blue (470nm)" current=0.030A package="5 mm [THT]"]
  LED6 = LED - 5mm [color="Yellow (585nm)" current=0.030A package="5 mm [THT]"]
  OLED_I2C2 = OLED 128x64 I2C Monochrome Display
  LED7 = LED - 5mm [color="Blue (470nm)" current=0.030A package="5 mm [THT]"]
  LED8 = LED - 5mm [color="Yellow (592nm)" current=0.030A package="5 mm [THT]"]
  U1 = WS2812 RGB LED strip

nets:
  3.3V: A1.Pin_2, S8.Pin_3, S8.Pin_4, S10.Pin_3, S10.Pin_4, OLED_I2C1.VDD, S11.L2, OLED_I2C2.VDD
  GND: A1.Pin_4, A1.Pin_30, S5.Pin_3, S5.Pin_4, Part1.GND, Part2.GND, Neopixel2.G, OLED_I2C1.GND, S11.L1, S12.Pin_3, S12.Pin_4, LED1.cathode, LED2.cathode, LED3.cathode, LED4.cathode, Neopixel1.G, LED5.cathode, LED6.cathode, OLED_I2C2.GND, LED7.cathode, LED8.cathode, U1.GND
  N1: A1.Pin_5, S5.Pin_1, S5.Pin_2
  N2: A1.Pin_6, S12.Pin_1, S12.Pin_2
  N3: A1.Pin_7, S7.Pin_1, S7.Pin_2
  N4: A1.Pin_8, S9.Pin_1, S9.Pin_2
  N5: A1.Pin_9, LED5.anode
  N6: A1.Pin_10, LED6.anode
  N7: A1.Pin_11, S11.COM
  N8: A1.Pin_17, OLED_I2C1.SDA, OLED_I2C2.SDA
  N9: A1.Pin_18, OLED_I2C1.SCK, OLED_I2C2.SCK
  N10: A1.Pin_19, Neopixel1.In, U1.DIN
  N11: A1.Pin_20, Part2.OUT, LED7.anode
  N12: A1.Pin_23, A1.Pin_37, LED2.anode, LED3.anode
  N13: A1.Pin_24, A1.Pin_36, LED1.anode, LED4.anode
  N14: A1.Pin_25, Part1.OUT, LED8.anode
  5V: A1.Pin_26, Part1.VCC, Part2.VCC, Neopixel2.+, Neopixel1.+, U1.VCC
  N15: S7.Pin_3, S7.Pin_4, S8.Pin_1, S8.Pin_2
  N16: S9.Pin_3, S9.Pin_4, S10.Pin_1, S10.Pin_2
  N17: Neopixel2.In, Neopixel1.O

notes:
  2 buttons for each player to place their hand before each round starts.
  LEDs built into buttons
  Switch to toggle between manual/automatic
  One motion sensor pointed at each player. LEDs connected directly to PIR sensors to show any motion regardless of program.
  The button each player is trying to press. Arcade buttons with LEDs builtin.
  White LEDs represent the LEDs inside the white arcade "Ready" buttons.
  Blue and Yellow LEDs are wired to the output of the motion sensors to show when they detect motion before they interact with any code.
  These black buttons represent the white arcade "Ready" buttons. They are all wired in series so the game only starts when all 4 are pushed.
  These are the large blue and yellow (gold) arcade buttons that each player is trying to press. The blue and yellow LEDs here represent LEDs inside each arcade button.
  PIR sensors provided more reliable signals when wired into 5V instead of 3.3V like most other components.

custom parts:
  Particle - Photon2: The Photon 2 is a microcontroller and Wi-Fi networking developed by particle. Features: 802.11a/b/g/n Wi-Fi, 2.4 GHz and 5 GHz Integrated PCB antenna Integrated U.FL connector for external antenna Integrated RF switch BLE 5 using same antenna as Wi-Fi Realtek RTL8721DM MCU ARM Cortex M33 CPU, 200 MHz 2048 KB (2 MB) user application maximum size 3072 KB (3 MB) of RAM available to user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
  Pushbutton: A generic pushbutton.
  Pushbutton: A generic pushbutton.
  HC-SR501 Body Sensor Module: Pyroelectric Infrared PIR Motion Sensor Detector Module
  Pushbutton: A generic pushbutton.
  WS2812 RGB LED strip: WS2812 strip
